// Logisim project CircuitoIntegrado.circ as structural Verilog: 1 circuit, main circuit main
module main (
  input  [15:0] Instruction_In,
  output [2:0] out_2,
  output [3:0] \Cálculo_do_jump ,
  output [3:0] Debug_RA,
  output [3:0] out_5,
  output [3:0] Debug_ULA,
  output [3:0] Debug_PC,
  output [15:0] Debug_IM
);

  wire comparator_1_eq, Uc_clock_ir, Uc_clock_pc, Uc_clock_r0, Uc_clock_r1, Uc_clock_ra,
       Uc_select_input_mux_mem, Uc_select_input_mux_ula, Uc_write_mem;
  wire [3:0] multiplexer_1_out, R0_data_out, R1_data_out;
  wire [15:0] main_1_out_3, multiplexer_2_out;

  Register RA (.Data_In(Instruction_In[3:0]), .Clock(Uc_clock_ra), .Data_Out(Debug_RA));
  Register PC (.Data_In(\Cálculo_do_jump ), .Clock(Uc_clock_pc), .Data_Out(Debug_PC));
  Multiplexer #(.width(4), .enable("false")) multiplexer_1 (
    .in0(Debug_RA), .in1(Debug_PC), .out(multiplexer_1_out), .sel(Uc_select_input_mux_mem));
  Bit_Extender #(.in_width(4)) bit_extender_1 (.in(Debug_ULA));  // open: out
  Instruction_Memory IM (
    .Data_to_Save(Instruction_In), .Data_to_Read(Debug_IM), .Adress_to_Write(multiplexer_1_out),
    .Write_State(Uc_clock_ir), .Adress_to_Read(multiplexer_1_out));
  IR_main main_1 (.in_2(Debug_IM), .in_1(Uc_clock_ir), .out_3(main_1_out_3));
  Multiplexer #(.width(16), .enable("false")) multiplexer_2 (
    .in0(main_1_out_3), .in1({16{1'b0}}), .out(multiplexer_2_out), .sel(Uc_select_input_mux_ula));
  Send_Signal Uc (
    .in_1(3'b001), .Decoded_Instruction(Instruction_In), .state(out_2), .Clock_IR(Uc_clock_ir),
    .Select_input_MUX_MEM(Uc_select_input_mux_mem), .Clock_PC(Uc_clock_pc), .Clock_RA(Uc_clock_ra),
    .Clock_R0(Uc_clock_r0), .Clock_R1(Uc_clock_r1), .Select_ULA_operation(out_5), .Write_MEM(Uc_write_mem),
    .Select_Input_MUX_ULA(Uc_select_input_mux_ula));
  Comparator #(.width(3)) comparator_1 (.a(3'b001), .b(3'b111), .eq(comparator_1_eq));  // open: gt, lt
  Register R0 (.Data_In(multiplexer_2_out[11:8]), .Clock(Uc_clock_r0), .Data_Out(R0_data_out));
  Register R1 (.Data_In(multiplexer_2_out[7:4]), .Clock(Uc_clock_r1), .Data_Out(R1_data_out));
  JumpDecoder_main JumperDecoder (
    .PC(Debug_PC), .RA(Debug_RA), .Is_Jump_Instruction(comparator_1_eq), .out_4(\Cálculo_do_jump ));
  ULA ula_1 (
    .Entry_A(R0_data_out), .Entry_B(R1_data_out), .Out(Debug_ULA), .OPCODE(out_5));  // open: Carry__iN, Carry_Out
endmodule
