// Logisim project JumpDecoder.circ as structural Verilog: 1 circuit, main circuit main
module main (
  input  [15:0] PC,
  input  [15:0] Instruction,
  output [15:0] out_3
);


  assign out_3 = {4'b0000, PC[15:12], Instruction[7:0]};

  // Notes on the sheet:
  //   Cálculo do jump : 4 bits mais significativos do pc + endereço da instrução + 0000
endmodule
